# Fritzing sketch Rain (saved by Fritzing 0.9.3b)

parts:
  Часть1 = Arduino Uno (Rev3)
  Часть2 = LCD1602-I2C
  YL-83_-_Control_Board1 = YL-83 Rain Sensor - Control Board
  YL-83_-_Detection_Board1 = YL-83 Rain Sensor - Detection Board

nets:
  N1: Часть1.A0, YL-83_-_Control_Board1.AO
  N2: Часть1.A4/SDA, Часть2.SDA
  N3: Часть1.A5/SCL, Часть2.SCL
  VCC: Часть1.5V, Часть2.VCC, YL-83_-_Control_Board1.VCC
  GND: Часть1.GND, Часть2.GND, YL-83_-_Control_Board1.GND
  N4: YL-83_-_Control_Board1.POS, YL-83_-_Detection_Board1.NEG
  N5: YL-83_-_Control_Board1.NEG, YL-83_-_Detection_Board1.POS

custom parts:
  LCD1602-I2C: A standard character display, usually with 2x16 characters. Comes in many colors with LCM1602 IIC attached.
  YL-83 Rain Sensor - Control Board: The YL-83 is a rain sensor that has more resistance when dry and less resistance when wet. The module runs at 5V.
  YL-83 Rain Sensor - Detection Board: The YL-83 is a rain sensor that has more resistance when dry and less resistance when wet. The module runs at 5V.
